# Fritzing sketch Arduino pov fritzing (saved by Fritzing 0.9.3b)
circuit board: 20.6609cm x 4cm
breadboards: 1

parts:
  Arduino_Nano = Arduino Nano v2.3
  +_- = Header 2 [package=screwterminal-3.5mm-2_lock]
  BT_HC-05 = Bluetooth HC-05 Macho
  LED2 = LED - 5mm [color="Red (633nm)" package="5 mm [THT]"]
  LED3 = LED - 5mm [color="Red (633nm)" package="5 mm [THT]"]
  LED4 = LED - 5mm [color="Red (633nm)" package="5 mm [THT]"]
  LED5 = LED - 5mm [color="Red (633nm)" package="5 mm [THT]"]
  LED6 = LED - 5mm [color="Red (633nm)" package="5 mm [THT]"]
  LED7 = LED - 5mm [color="Red (633nm)" package="5 mm [THT]"]
  330 = Resistor [tolerance=±5% resistance=220 package=THT]
  330_2 = Resistor [tolerance=±5% resistance=220 package=THT]
  330_3 = Resistor [tolerance=±5% resistance=220 package=THT]
  330_4 = Resistor [tolerance=±5% resistance=220 package=THT]
  330_5 = Resistor [tolerance=±5% resistance=220 package=THT]
  330_6 = Resistor [tolerance=±5% resistance=220 package=THT]
  330_7 = Resistor [tolerance=±5% resistance=220 package=THT]
  +IR- = LTE-302 [package=lte-302]
  +PD- = LTE-302 [package=lte-302]
  IR_330 = Resistor [tolerance=±5% resistance=220 package=THT]
  PD_10K = Resistor [tolerance=±5% resistance=220 package=THT]
  LED1 = LED - 5mm [color="Red (633nm)" package="5 mm [THT]"]
  S1 = SPST Switch [package=switch-spdt-smd]

nets:
  GND: Arduino_Nano.GND, +_-.2, BT_HC-05.GND, 330.Pin_1, 330_2.Pin_1, 330_3.Pin_1, 330_4.Pin_1, 330_5.Pin_1, 330_6.Pin_1, 330_7.Pin_1, +IR-.A, PD_10K.Pin_0
  N1: Arduino_Nano.D4, LED7.anode
  N2: Arduino_Nano.D5, LED6.anode
  N3: Arduino_Nano.D6, LED5.anode
  N4: Arduino_Nano.D7, LED4.anode
  N5: Arduino_Nano.D8, LED3.anode
  N6: Arduino_Nano.D9, LED2.anode
  N7: Arduino_Nano.D10, LED1.anode
  N8: Arduino_Nano.D11, BT_HC-05.TXD
  N9: Arduino_Nano.D12, BT_HC-05.RXD
  N10: Arduino_Nano.A7, +PD-.C, PD_10K.Pin_1
  +5V: Arduino_Nano.+5V, BT_HC-05.VCC, +PD-.A, IR_330.Pin_0
  N11: Arduino_Nano.VIN, S1.S
  N12: +_-.1, S1.P
  N13: LED2.cathode, 330_2.Pin_0
  N14: LED3.cathode, 330_3.Pin_0
  N15: LED4.cathode, 330_4.Pin_0
  N16: LED5.cathode, 330_5.Pin_0
  N17: LED6.cathode, 330_6.Pin_0
  N18: LED7.cathode, 330_7.Pin_0
  N19: 330.Pin_0, LED1.cathode
  N20: +IR-.C, IR_330.Pin_1
